// Logisim project fsm_next_state_logic.circ as structural Verilog: 2 circuits, main circuit main
module main (
  input  m_2,
  input  m_1,
  input  m_0,
  input  l
);

  wire and_1_out, logic_1_v_0, logic_1_v_1, logic_1_v_2, logic_1_v_3, not_1_out, not_2_out;

  \logic  logic_1 (
    .m_2(m_2), .m_1(m_1), .m_0(m_0), .l(l), .p_3(logic_1_v_3), .p_2(logic_1_v_2), .p_1(logic_1_v_1),
    .p_0(logic_1_v_0), .v_3(logic_1_v_3), .v_2(logic_1_v_2), .v_1(logic_1_v_1), .v_0(logic_1_v_0));
  not not_1 (not_1_out, logic_1_v_2);
  not not_2 (not_2_out, logic_1_v_1);
  and and_1 (and_1_out, logic_1_v_3, not_1_out, not_2_out, logic_1_v_0);
  LED led_1 (.in(and_1_out));
endmodule

module \logic  (
  input  m_2,
  input  m_1,
  input  m_0,
  input  l,
  input  p_3,
  input  p_2,
  input  p_1,
  input  p_0,
  output v_3,
  output v_2,
  output v_1,
  output v_0
);

  wire and_1_out, and_2_out, and_3_out, and_4_out, and_5_out, and_6_out, and_7_out, not_1_out, not_2_out,
       not_3_out, not_4_out, not_5_out, not_6_out, not_7_out, not_8_out, not_9_out, not_10_out, not_11_out,
       not_12_out, not_13_out, not_14_out, not_15_out, not_16_out, not_17_out;

  not not_1 (not_1_out, p_3);
  not not_2 (not_2_out, p_0);
  and and_1 (and_1_out, not_2_out, l);
  not not_3 (not_3_out, p_2);
  not not_4 (not_4_out, p_1);
  not not_5 (not_5_out, l);
  not not_6 (not_6_out, p_2);
  not not_7 (not_7_out, p_1);
  not not_8 (not_8_out, p_2);
  not not_9 (not_9_out, p_1);
  not not_10 (not_10_out, l);
  not not_11 (not_11_out, p_2);
  not not_12 (not_12_out, p_1);
  not not_13 (not_13_out, p_2);
  not not_14 (not_14_out, p_1);
  not not_15 (not_15_out, p_0);
  not not_16 (not_16_out, p_2);
  not not_17 (not_17_out, p_1);
  or or_1 (v_3, not_1_out, and_1_out, p_1, p_2);
  and and_2 (and_2_out, p_3, not_3_out, not_4_out, m_2, not_5_out);
  or or_2 (v_2, and_2_out, and_3_out);
  and and_3 (and_3_out, p_3, not_6_out, not_7_out, p_0, m_2);
  and and_4 (and_4_out, p_3, not_8_out, not_9_out, m_1, not_10_out);
  or or_3 (v_1, and_4_out, and_5_out);
  and and_5 (and_5_out, p_3, not_11_out, not_12_out, p_0, m_1);
  and and_6 (and_6_out, p_3, not_13_out, not_14_out, not_15_out, l);
  or or_4 (v_0, and_6_out, and_7_out);
  and and_7 (and_7_out, p_3, not_16_out, not_17_out, m_0);
endmodule
