// Logisim project 21347021.circ as structural Verilog: 3 circuits, main circuit main
module main (
  input  a_1,
  input  a_0,
  input  b_1,
  input  b_0
);

  wire led_control_1_a_wins, led_control_1_b_wins, rpls_1_w_0, rpls_1_w_1;

  rpls rpls_1 (.a_1(a_1), .a_0(a_0), .b_1(b_1), .b_0(b_0), .w_1(rpls_1_w_1), .w_0(rpls_1_w_0));
  LED A_wins (.in(led_control_1_a_wins));
  led_control led_control_1 (
    .w_1(rpls_1_w_1), .w_0(rpls_1_w_0), .A_wins(led_control_1_a_wins), .B_wins(led_control_1_b_wins));
  LED B_wins (.in(led_control_1_b_wins));
endmodule

module rpls (
  input  a_1,
  input  a_0,
  input  b_1,
  input  b_0,
  output w_1,
  output w_0
);

  wire and_1_out, and_2_out, and_3_out, and_4_out, and_5_out, and_6_out, and_7_out, and_8_out, and_9_out,
       and_10_out, not_1_out, not_2_out, not_3_out, not_4_out, not_5_out, not_6_out, not_7_out, not_8_out,
       not_9_out, not_10_out, not_11_out, not_12_out, not_13_out, not_14_out, not_15_out, not_16_out;

  not not_1 (not_1_out, a_1);
  not not_2 (not_2_out, a_0);
  not not_3 (not_3_out, b_0);
  not not_4 (not_4_out, a_0);
  not not_5 (not_5_out, b_1);
  not not_6 (not_6_out, b_0);
  not not_7 (not_7_out, b_1);
  not not_8 (not_8_out, a_0);
  not not_9 (not_9_out, b_1);
  not not_10 (not_10_out, b_0);
  not not_11 (not_11_out, a_1);
  not not_12 (not_12_out, a_0);
  not not_13 (not_13_out, b_1);
  not not_14 (not_14_out, b_0);
  not not_15 (not_15_out, a_0);
  not not_16 (not_16_out, b_0);
  and and_1 (and_1_out, not_1_out, not_2_out, b_0);
  and and_2 (and_2_out, a_0, b_1, not_3_out);
  and and_3 (and_3_out, a_1, not_4_out, not_5_out, not_6_out);
  and and_4 (and_4_out, a_1, a_0, not_7_out, b_0);
  and and_5 (and_5_out, not_8_out, not_9_out, not_10_out);
  and and_6 (and_6_out, not_11_out, not_12_out, b_0);
  and and_7 (and_7_out, a_0, not_13_out, b_0);
  and and_8 (and_8_out, a_0, b_1, not_14_out);
  and and_9 (and_9_out, a_1, not_15_out, not_16_out);
  and and_10 (and_10_out, a_1, a_0, b_1);
  or or_1 (w_1, and_1_out, and_2_out, and_3_out, and_4_out);
  or or_2 (w_0, and_5_out, and_6_out, and_7_out, and_8_out, and_9_out, and_10_out);
endmodule

module led_control (
  input  w_1,
  input  w_0,
  output A_wins,
  output B_wins
);

  wire not_1_out, not_2_out;

  not not_1 (not_1_out, w_1);
  not not_2 (not_2_out, w_0);
  and and_1 (A_wins, not_1_out, not_2_out);
  and and_2 (B_wins, w_1, w_0);
endmodule
